# Fritzing sketch LED_Group_Perfboard (saved by Fritzing 0.9.2b)
perfboards: 1

parts:
  U1 = Packages: [package=dil28-3]
  U2 = Packages: [package=dil28-3]
  C3 = Ceramic Capacitor [capacitance=0.1µF package="100 mil [THT, multilayer]"]
  R1 = Resistor [tolerance=±5% resistance=1.91k package=THT]
  R2 = Resistor [tolerance=±5% resistance=1.91k package=THT]
  LED1 = RGB LED - (4 legs) [package="5 mm [THT]"]
  LED10 = LED - 5mm [color="Infrared (940nm)" package="5 mm [THT]"]
  C1 = Ceramic Capacitor [capacitance=0.1µF package="100 mil [THT, multilayer]"]
  C2 = Ceramic Capacitor [capacitance=0.1µF package="100 mil [THT, multilayer]"]
  J1 = female pin header, 4 pins [form="♀ (female)"]
  J11 = female pin header, 5 pins [form="♀ (female)"]
  J12 = female pin header, 5 pins [form="♀ (female)"]
  LED2 = RGB LED - (4 legs) [package="5 mm [THT]"]
  J2 = female pin header, 4 pins [form="♀ (female)"]
  LED3 = RGB LED - (4 legs) [package="5 mm [THT]"]
  J3 = female pin header, 4 pins [form="♀ (female)"]
  LED4 = RGB LED - (4 legs) [package="5 mm [THT]"]
  J4 = female pin header, 4 pins [form="♀ (female)"]
  LED5 = RGB LED - (4 legs) [package="5 mm [THT]"]
  J5 = female pin header, 4 pins [form="♀ (female)"]
  LED6 = RGB LED - (4 legs) [package="5 mm [THT]"]
  J6 = female pin header, 4 pins [form="♀ (female)"]
  LED7 = RGB LED - (4 legs) [package="5 mm [THT]"]
  J7 = female pin header, 4 pins [form="♀ (female)"]
  LED8 = RGB LED - (4 legs) [package="5 mm [THT]"]
  J8 = female pin header, 4 pins [form="♀ (female)"]
  LED9 = RGB LED - (4 legs) [package="5 mm [THT]"]
  J9 = female pin header, 4 pins [form="♀ (female)"]
  R3 = Resistor [tolerance=±5% resistance=75 package=THT]
  J10 = female pin header, 5 pins [form="♀ (female)"]
  IR1 = TSOP312.., 314.. [package=THT]

nets:
  N1: U1.OUT1, LED1.green_cathode, J1.pin3
  N2: U1.OUT2, LED1.blue_cathode, J1.pin4
  N3: U1.OUT3, LED2.red_cathode, J2.pin2
  N4: U1.OUT4, LED2.green_cathode, J2.pin3
  N5: U1.OUT5, LED2.blue_cathode, J2.pin4
  N6: U1.OUT6, LED3.red_cathode, J3.pin2
  N7: U1.OUT7, LED3.green_cathode, J3.pin3
  N8: U1.OUT8, LED3.blue_cathode, J3.pin4
  N9: U1.OUT9, LED4.red_cathode, J4.pin2
  N10: U1.OUT10, LED4.green_cathode, J4.pin3
  N11: U1.OUT11, LED4.blue_cathode, J4.pin4
  N12: U1.OUT12, LED5.red_cathode, J5.pin2
  N13: U1.OUT13, LED5.green_cathode, J5.pin3
  N14: U1.OUT14, LED5.blue_cathode, J5.pin4
  N15: U1.SOUT, U2.SIN
  N16: U1.GSCLK, J11.pin5
  5V: U1.DCPRG, U1.VCC, U2.DCPRG, U2.VCC, C3.1, LED1.common_anode, LED10.anode, C1.1, C2.1, J1.pin1, LED2.common_anode, J2.pin1, LED3.common_anode, J3.pin1, LED4.common_anode, J4.pin1, LED5.common_anode, J5.pin1, LED6.common_anode, J6.pin1, LED7.common_anode, J7.pin1, LED8.common_anode, J8.pin1, LED9.common_anode, J9.pin1, R3.Pin_0, J10.pin1
  N17: U1.IREF, R1.Pin_1
  GND: U1.GND, U2.GND, C3.0, R1.Pin_0, R2.Pin_0, C1.0, C2.0, J10.pin5, IR1.GND
  N18: U1.BLANK, J11.pin1
  N19: U1.XLAT, J11.pin4
  N20: U1.SCLK, J11.pin2
  N21: U1.SIN, J11.pin3
  N22: U1.OUT0, LED1.red_cathode, J1.pin2
  N23: U2.OUT1, LED6.green_cathode, J6.pin3
  N24: U2.OUT2, LED6.blue_cathode, J6.pin4
  N25: U2.OUT3, LED7.red_cathode, J7.pin2
  N26: U2.OUT4, LED7.green_cathode, J7.pin3
  N27: U2.OUT5, LED7.blue_cathode, J7.pin4
  N28: U2.OUT6, LED8.red_cathode, J8.pin2
  N29: U2.OUT7, LED8.green_cathode, J8.pin3
  N30: U2.OUT8, LED8.blue_cathode, J8.pin4
  N31: U2.OUT9, LED9.red_cathode, J9.pin2
  N32: U2.OUT10, LED9.green_cathode, J9.pin3
  N33: U2.OUT11, LED9.blue_cathode, J9.pin4
  N34: U2.SOUT, J12.pin3
  N35: U2.GSCLK, J12.pin5
  N36: U2.IREF, R2.Pin_1
  N37: U2.BLANK, J12.pin1
  N38: U2.XLAT, J12.pin4
  N39: U2.SCLK, J12.pin2
  N40: U2.OUT0, LED6.red_cathode, J6.pin2
  N41: LED10.cathode, J10.pin2
  N42: R3.Pin_1, J10.pin3, IR1.Vs
  N43: J10.pin4, IR1.Data

notes:
  Input
  Output
  PWR&IR
  LED1
  LED2
  LED3
  LED5
  LED4
  LED6
  LED7
  LED8
  LED9
